// Digital circuit add_sub_via_instruction.dig as structural Verilog
module add_sub_via_instruction (
  input  [6:0] Instruction,
  input  clk,
  input  in_3,
  output [3:0] Sum,
  output [2:0] Diff
);

  wire [5:0] demultiplexer_1_out_0, demultiplexer_1_out_1;
  wire [6:0] register_1_q;

  Register #(.Bits(7)) register_1 (.D(Instruction), .C(clk), .en(in_3), .Q(register_1_q));
  Demultiplexer #(.Bits(6)) demultiplexer_1 (
    .sel(register_1_q[6]), .in(register_1_q[5:0]), .out_0(demultiplexer_1_out_0),
    .out_1(demultiplexer_1_out_1));
  Add #(.Bits(3)) add_1 (
    .a(demultiplexer_1_out_0[2:0]), .b(demultiplexer_1_out_0[5:3]), .c_i(1'b0), .s(Sum[2:0]), .c_o(Sum[3]));
  Sub #(.Bits(3)) sub_1 (
    .a(demultiplexer_1_out_1[2:0]), .b(demultiplexer_1_out_1[5:3]), .c_i(1'b0), .s(Diff));  // open: c_o
endmodule
