// Digital circuit addition_via_instruction.dig as structural Verilog
module addition_via_instruction (
  input  [6:0] Instruction,
  input  clk,
  input  in_3,
  output [3:0] Sum
);

  wire [6:0] register_1_q;

  Register #(.Bits(7)) register_1 (.D(Instruction), .C(clk), .en(in_3), .Q(register_1_q));
  Add #(.Bits(3)) add_1 (.a(register_1_q[2:0]), .b(register_1_q[5:3]), .c_i(1'b0), .s(Sum[2:0]), .c_o(Sum[3]));
  // also tied to GND on the sheet: register_1_q[6]
endmodule
