// Digital circuit counter.dig as structural Verilog
module counter (
  input  in_1,
  input  clk,
  input  in_5,
  output [1:0] out_2,
  output out_3
);

  Counter #(.Bits(2)) counter_1 (.en(in_1), .C(clk), .clr(in_5), .out(out_2), .ovf(out_3));
endmodule
